// Logisim project Maksim_Maksimov_1.2.circ as structural Verilog: 2 circuits, main circuit main
module main (
  input  a,
  input  b,
  input  c,
  output f
);

  wire and_1_out, and_2_out, nand_1_out, not_1_out;

  not not_1 (not_1_out, a);
  nand nand_1 (nand_1_out, not_1_out, b);
  and and_1 (and_1_out, b, c);
  and and_2 (and_2_out, not_1_out, c);
  or or_1 (f, nand_1_out, and_1_out, and_2_out);
endmodule

module dv (
  input  a,
  input  b,
  input  c,
  output f
);

  wire not_1_out;

  not not_1 (not_1_out, b);
  or or_1 (f, a, c, not_1_out);
endmodule
