// Logisim project Maksim_Maksimov2_1.circ as structural Verilog: 1 circuit, main circuit main
module main (
  input  x1,
  input  x2,
  input  x3,
  input  x4,
  output f
);

  wire and_1_out, and_2_out, nand_1_out, nand_2_out, not_1_out, or_1_out;

  not not_1 (not_1_out, x4);
  nand nand_1 (nand_1_out, x1, x3);
  and and_1 (and_1_out, nand_1_out, not_1_out);
  or or_1 (or_1_out, and_1_out, x1);
  and and_2 (and_2_out, x2, or_1_out);
  nand nand_2 (nand_2_out, x2, x3);
  or or_2 (f, and_2_out, nand_2_out);
endmodule
