// Logisim project Maksim_Maksimov4_2.circ as structural Verilog: 1 circuit, main circuit main
module main (
  input  x1,
  input  x2,
  input  x3,
  output y0,
  output y1,
  output y2,
  output y3,
  output y4,
  output y5,
  output y6,
  output y7
);

  wire not_1_out, not_2_out, not_3_out;

  not not_1 (not_1_out, x1);
  not not_2 (not_2_out, x2);
  not not_3 (not_3_out, x3);
  and and_1 (y0, not_3_out, x2, not_1_out);
  and and_2 (y1, not_3_out, not_2_out, not_1_out);
  and and_3 (y2, x3, x2, x1);
  and and_4 (y3, x3, not_2_out, x1);
  and and_5 (y4, x3, x2, not_1_out);
  and and_6 (y5, not_3_out, x2, x1);
  and and_7 (y6, not_3_out, not_2_out, x1);
  and and_8 (y7, x3, not_2_out, not_1_out);
endmodule
