// Logisim project Maksim_Maksimov_5.1.circ as structural Verilog: 2 circuits, main circuit main
module main (
  input  a,
  input  b,
  input  c,
  input  d,
  input  d0,
  input  d1,
  input  d2,
  input  d3,
  input  d4,
  input  d5,
  input  d6,
  input  d7,
  input  d8,
  input  d9,
  input  d10,
  input  d11,
  input  d12,
  input  d13,
  input  d14,
  input  d15,
  output E
);

  wire and_1_out, and_2_out, and_3_out, and_4_out, and_5_out, and_6_out, and_7_out, and_8_out, and_9_out,
       and_10_out, and_11_out, and_12_out, and_13_out, and_14_out, and_15_out, and_16_out, and_17_out,
       and_18_out, and_19_out, and_20_out, and_21_out, and_22_out, and_23_out, and_24_out, and_25_out,
       and_26_out, and_27_out, and_28_out, and_29_out, and_30_out, and_31_out, and_32_out, not_1_out,
       not_2_out, not_3_out, not_4_out;

  not not_1 (not_1_out, a);
  not not_2 (not_2_out, b);
  not not_3 (not_3_out, c);
  not not_4 (not_4_out, d);
  and and_1 (and_1_out, not_1_out, not_2_out, not_3_out, not_4_out);
  and and_2 (and_2_out, and_1_out, d0);
  and and_3 (and_3_out, not_1_out, not_2_out, not_3_out, d);
  and and_4 (and_4_out, and_3_out, d1);
  and and_5 (and_5_out, not_1_out, not_2_out, c, not_4_out);
  and and_6 (and_6_out, and_5_out, d2);
  and and_7 (and_7_out, not_1_out, not_2_out, c, d);
  and and_8 (and_8_out, and_7_out, d3);
  and and_9 (and_9_out, not_1_out, b, not_3_out, not_4_out);
  and and_10 (and_10_out, and_9_out, d4);
  and and_11 (and_11_out, not_1_out, b, not_3_out, d);
  and and_12 (and_12_out, and_11_out, d5);
  and and_13 (and_13_out, not_1_out, b, c, not_4_out);
  and and_14 (and_14_out, and_13_out, d6);
  and and_15 (and_15_out, not_1_out, b, c, d);
  and and_16 (and_16_out, and_15_out, d7);
  and and_17 (and_17_out, a, not_2_out, not_3_out, not_4_out);
  and and_18 (and_18_out, and_17_out, d8);
  and and_19 (and_19_out, a, not_2_out, not_3_out, d);
  and and_20 (and_20_out, and_19_out, d9);
  and and_21 (and_21_out, a, not_2_out, c, not_4_out);
  and and_22 (and_22_out, and_21_out, d10);
  and and_23 (and_23_out, a, not_2_out, c, d);
  and and_24 (and_24_out, and_23_out, d11);
  and and_25 (and_25_out, a, b, not_3_out, not_4_out);
  and and_26 (and_26_out, and_25_out, d12);
  and and_27 (and_27_out, a, b, not_3_out, d);
  and and_28 (and_28_out, and_27_out, d13);
  and and_29 (and_29_out, a, b, c, not_4_out);
  and and_30 (and_30_out, and_29_out, d14);
  and and_31 (and_31_out, a, b, c, d);
  and and_32 (and_32_out, and_31_out, d15);
  or or_1 (E, and_2_out, and_4_out, and_6_out, and_8_out, and_10_out, and_12_out, and_14_out, and_16_out, and_18_out, and_20_out, and_22_out, and_24_out, and_26_out, and_28_out, and_30_out, and_32_out);
endmodule

module main2 (
  input  a,
  input  b,
  input  c,
  input  d,
  output x0,
  output x1,
  output x2,
  output x3,
  output x4,
  output x5,
  output x6,
  output x7,
  output x8,
  output x9,
  output x10,
  output x11,
  output x12,
  output x13,
  output x14,
  output x15
);

  wire not_1_out, not_2_out, not_3_out, not_4_out;

  not not_1 (not_1_out, a);
  not not_2 (not_2_out, b);
  not not_3 (not_3_out, c);
  not not_4 (not_4_out, d);
  and and_1 (x0, not_1_out, not_2_out, not_3_out, not_4_out, 1'b0);
  and and_2 (x1, not_1_out, not_2_out, not_3_out, d, 1'b0);
  and and_3 (x2, not_1_out, not_2_out, c, not_4_out, 1'b1);
  and and_4 (x3, not_1_out, not_2_out, c, d, 1'b1);
  and and_5 (x4, not_1_out, b, not_3_out, not_4_out, 1'b0);
  and and_6 (x5, not_1_out, b, not_3_out, d, 1'b0);
  and and_7 (x6, not_1_out, b, c, not_4_out, 1'b1);
  and and_8 (x7, not_1_out, b, c, d, 1'b1);
  and and_9 (x8, a, not_2_out, not_3_out, not_4_out, 1'b0);
  and and_10 (x9, a, not_2_out, not_3_out, d, 1'b1);
  and and_11 (x10, a, not_2_out, c, not_4_out, 1'b1);
  and and_12 (x11, a, not_2_out, c, d, 1'b0);
  and and_13 (x12, a, b, not_3_out, not_4_out, 1'b0);
  and and_14 (x13, a, b, not_3_out, d, 1'b1);
  and and_15 (x14, a, b, c, not_4_out, 1'b0);
  and and_16 (x15, a, b, c, d, 1'b1);
endmodule
