// Logisim project Maksim_Maksimov_5.2.circ as structural Verilog: 1 circuit, main circuit main
module main (
  input  a,
  input  b,
  input  c,
  input  d,
  output y0,
  output y1,
  output y2,
  output y3,
  output y4,
  output y5,
  output y6,
  output y7,
  output y8,
  output y9,
  output y10,
  output y11,
  output y12,
  output y13,
  output y14,
  output y15
);

  wire not_1_out, not_2_out, not_3_out, not_4_out;

  not not_1 (not_1_out, a);
  not not_2 (not_2_out, b);
  not not_3 (not_3_out, c);
  not not_4 (not_4_out, d);
  and and_1 (y0, not_1_out, not_2_out, not_3_out, not_4_out, 1'b0);
  and and_2 (y1, not_1_out, not_2_out, not_3_out, d, 1'b1);
  and and_3 (y2, not_1_out, not_2_out, c, not_4_out, 1'b0);
  and and_4 (y3, not_1_out, not_2_out, c, d, 1'b1);
  and and_5 (y4, not_1_out, b, not_3_out, not_4_out, 1'b0);
  and and_6 (y5, not_1_out, b, not_3_out, d, 1'b0);
  and and_7 (y6, not_1_out, b, c, not_4_out, 1'b0);
  and and_8 (y7, not_1_out, b, c, d, 1'b1);
  and and_9 (y8, a, not_2_out, not_3_out, not_4_out, 1'b0);
  and and_10 (y9, a, not_2_out, not_3_out, d, 1'b1);
  and and_11 (y10, a, not_2_out, c, not_4_out, 1'b1);
  and and_12 (y11, a, not_2_out, c, d, 1'b0);
  and and_13 (y12, a, b, not_3_out, not_4_out, 1'b0);
  and and_14 (y13, a, b, not_3_out, d, 1'b1);
  and and_15 (y14, a, b, c, not_4_out, 1'b0);
  and and_16 (y15, a, b, c, d, 1'b1);
endmodule
