// Logisim project prac5_2.circ as structural Verilog: 1 circuit, main circuit main
module main (
  input  E,
  input  a,
  input  b,
  input  c,
  input  d,
  output d0,
  output d1,
  output d2,
  output d3,
  output d4,
  output d5,
  output d6,
  output d7,
  output d8,
  output d9,
  output d10,
  output d11,
  output d12,
  output d13,
  output d14,
  output d15
);

  wire not_1_out, not_2_out, not_3_out, not_4_out;

  not not_1 (not_1_out, a);
  not not_2 (not_2_out, b);
  not not_3 (not_3_out, c);
  not not_4 (not_4_out, d);
  and and_1 (d0, E, not_1_out, not_2_out, not_3_out, not_4_out);
  and and_2 (d1, E, not_1_out, not_2_out, not_3_out, d);
  and and_3 (d2, E, not_1_out, not_2_out, c, not_4_out);
  and and_4 (d3, E, not_1_out, not_2_out, c, d);
  and and_5 (d4, E, not_1_out, b, not_3_out, not_4_out);
  and and_6 (d5, E, not_1_out, b, not_3_out, d);
  and and_7 (d6, E, not_1_out, b, c, not_4_out);
  and and_8 (d7, E, not_1_out, b, c, d);
  and and_9 (d8, E, a, not_2_out, not_3_out, not_4_out);
  and and_10 (d9, E, a, not_2_out, not_3_out, d);
  and and_11 (d10, E, a, not_2_out, c, not_4_out);
  and and_12 (d11, E, a, not_2_out, c, d);
  and and_13 (d12, E, a, b, not_3_out, not_4_out);
  and and_14 (d13, E, a, b, not_3_out, d);
  and and_15 (d14, E, a, b, c, not_4_out);
  and and_16 (d15, E, a, b, c, d);
endmodule
