// Logisim project Maksim_Maksimov_6.2.circ as structural Verilog: 1 circuit, main circuit main
module main (
  input  S,
  input  R
);

  wire C_out, nand_1_out, nand_2_out, nand_3_out, nand_4_out;

  Clock C (.out(C_out));
  nand nand_1 (nand_1_out, S, C_out);
  nand nand_2 (nand_2_out, C_out, R);
  nand nand_3 (nand_3_out, nand_1_out, nand_4_out);
  nand nand_4 (nand_4_out, nand_3_out, nand_2_out);
  // Probe on nand_3_out
  // Probe on nand_4_out
  // Digital_Oscilloscope digital_oscilloscope_1: pin names not known; wires that end beside it: C_out, S, R, nand_3_out
endmodule
