// Logisim project VT_6.1.circ as structural Verilog: 1 circuit, main circuit main
module main (
  input  R,
  input  S
);

  wire nor_1_out, nor_2_out;

  nor nor_1 (nor_1_out, R, nor_2_out);
  nor nor_2 (nor_2_out, S, nor_1_out);
  // Probe on nor_1_out
  // Probe on nor_2_out
endmodule
