// Logisim project VT_6.4.circ as structural Verilog: 1 circuit, main circuit main
module main (
  input  D
);

  wire C_out, nand_1_out, nand_2_out, nand_3_out, nand_4_out;

  Clock C (.out(C_out));
  nand nand_1 (nand_1_out, D, C_out);
  nand nand_2 (nand_2_out, nand_1_out, C_out);
  // Probe on nand_3_out
  nand nand_3 (nand_3_out, nand_1_out, nand_4_out);
  // Probe on nand_4_out
  nand nand_4 (nand_4_out, nand_3_out, nand_2_out);
  // Digital_Oscilloscope digital_oscilloscope_1: pin names not known; wires that end beside it: C_out, D, nand_3_out
endmodule
