// Logisim project VT_6.5.circ as structural Verilog: 1 circuit, main circuit main
module main (
  input  T
);

  wire and_1_out, C_out, nand_1_out, nand_2_out, nand_3_out, nand_4_out, nand_5_out, nand_6_out, nand_7_out,
       nand_8_out, not_1_out;

  Clock C (.out(C_out));
  and and_1 (and_1_out, T, nand_7_out);
  nand nand_1 (nand_1_out, and_1_out, C_out);
  nand nand_2 (nand_2_out, nand_1_out, C_out);
  not not_1 (not_1_out, C_out);
  nand nand_3 (nand_3_out, nand_1_out, nand_4_out);
  nand nand_4 (nand_4_out, nand_3_out, nand_2_out);
  nand nand_5 (nand_5_out, nand_4_out, not_1_out);
  nand nand_6 (nand_6_out, nand_5_out, not_1_out);
  nand nand_7 (nand_7_out, nand_5_out, nand_8_out);
  nand nand_8 (nand_8_out, nand_7_out, nand_6_out);
  // Probe on nand_7_out
  // Probe on nand_8_out
  // Digital_Oscilloscope digital_oscilloscope_1: pin names not known; wires that end beside it: C_out, nand_7_out
endmodule
