// Logisim project prac5_1.circ as structural Verilog: 1 circuit, main circuit main
module main (
  input  a,
  input  b,
  input  c,
  input  d,
  input  d0,
  input  d1,
  input  d2,
  input  d3,
  input  d4,
  input  d5,
  input  d6,
  input  d7,
  input  d8,
  input  d9,
  input  d10,
  input  d11,
  input  d12,
  input  d13,
  input  d14,
  input  d15,
  output E
);

  wire and_1_out, and_2_out, and_3_out, and_4_out, and_5_out, and_6_out, and_7_out, and_8_out, and_9_out,
       and_10_out, and_11_out, and_12_out, and_13_out, and_14_out, and_15_out, and_16_out, and_17_out,
       and_18_out, and_19_out, and_20_out, and_21_out, and_22_out, and_23_out, and_24_out, and_25_out,
       and_26_out, and_27_out, and_28_out, and_29_out, and_30_out, and_31_out, and_32_out, not_1_out,
       not_2_out, not_3_out, not_4_out;

  not not_1 (not_1_out, a);
  not not_2 (not_2_out, b);
  not not_3 (not_3_out, c);
  not not_4 (not_4_out, d);
  and and_1 (and_1_out, not_1_out, not_2_out, not_3_out, not_4_out);
  and and_2 (and_2_out, and_1_out, d0);
  and and_3 (and_3_out, not_1_out, not_2_out, not_3_out, d);
  and and_4 (and_4_out, and_3_out, d1);
  and and_5 (and_5_out, not_1_out, not_2_out, c, not_4_out);
  and and_6 (and_6_out, and_5_out, d2);
  and and_7 (and_7_out, not_1_out, not_2_out, c, d);
  and and_8 (and_8_out, and_7_out, d3);
  and and_9 (and_9_out, not_1_out, b, not_3_out, not_4_out);
  and and_10 (and_10_out, and_9_out, d4);
  and and_11 (and_11_out, not_1_out, b, not_3_out, d);
  and and_12 (and_12_out, and_11_out, d5);
  and and_13 (and_13_out, not_1_out, b, c, not_4_out);
  and and_14 (and_14_out, and_13_out, d6);
  and and_15 (and_15_out, not_1_out, b, c, d);
  and and_16 (and_16_out, and_15_out, d7);
  and and_17 (and_17_out, a, not_2_out, not_3_out, not_4_out);
  and and_18 (and_18_out, and_17_out, d8);
  and and_19 (and_19_out, a, not_2_out, not_3_out, d);
  and and_20 (and_20_out, and_19_out, d9);
  and and_21 (and_21_out, a, not_2_out, c, not_4_out);
  and and_22 (and_22_out, and_21_out, d10);
  and and_23 (and_23_out, a, not_2_out, c, d);
  and and_24 (and_24_out, and_23_out, d11);
  and and_25 (and_25_out, a, b, not_3_out, not_4_out);
  and and_26 (and_26_out, and_25_out, d12);
  and and_27 (and_27_out, a, b, not_3_out, d);
  and and_28 (and_28_out, and_27_out, d13);
  and and_29 (and_29_out, a, b, c, not_4_out);
  and and_30 (and_30_out, and_29_out, d14);
  and and_31 (and_31_out, a, b, c, d);
  and and_32 (and_32_out, and_31_out, d15);
  or or_1 (E, and_2_out, and_4_out, and_6_out, and_8_out, and_10_out, and_12_out, and_14_out, and_16_out, and_18_out, and_20_out, and_22_out, and_24_out, and_26_out, and_28_out, and_30_out, and_32_out);
endmodule
