// Logisim project prac5_alt.circ as structural Verilog: 1 circuit, main circuit main
module main (
  input  a,
  input  b,
  input  c,
  input  d,
  input  d0,
  input  d1,
  input  d2,
  input  d3,
  input  d4,
  input  d5,
  input  d6,
  input  d7,
  input  d8,
  input  d9,
  input  d10,
  input  d11,
  input  d12,
  input  d13,
  input  d14,
  input  d15,
  output out_21,
  output out_22,
  output out_23,
  output out_24,
  output out_25,
  output out_26,
  output out_27,
  output out_28,
  output out_29,
  output out_30,
  output out_31,
  output out_32,
  output out_33,
  output out_34,
  output out_35,
  output out_36
);

  wire and_1_out, and_2_out, and_3_out, and_4_out, and_5_out, and_6_out, and_7_out, and_8_out, and_9_out,
       and_10_out, and_11_out, and_12_out, and_13_out, and_14_out, and_15_out, and_16_out, and_17_out,
       and_18_out, and_19_out, and_20_out, and_21_out, and_22_out, and_23_out, and_24_out, and_25_out,
       and_26_out, and_27_out, and_28_out, and_29_out, and_30_out, and_31_out, and_32_out, not_1_out,
       not_2_out, not_3_out, not_4_out, not_5_out, not_6_out, not_7_out, not_8_out, or_1_out;

  not not_1 (not_1_out, a);
  not not_2 (not_2_out, b);
  not not_3 (not_3_out, c);
  not not_4 (not_4_out, d);
  and and_1 (and_1_out, not_1_out, not_2_out, not_3_out, not_4_out);
  and and_2 (and_2_out, and_1_out, d0);
  and and_3 (and_3_out, not_1_out, not_2_out, not_3_out, d);
  and and_4 (and_4_out, and_3_out, d1);
  and and_5 (and_5_out, not_1_out, not_2_out, c, not_4_out);
  and and_6 (and_6_out, and_5_out, d2);
  and and_7 (and_7_out, not_1_out, not_2_out, c, d);
  and and_8 (and_8_out, and_7_out, d3);
  and and_9 (and_9_out, not_1_out, b, not_3_out, not_4_out);
  and and_10 (and_10_out, and_9_out, d4);
  and and_11 (and_11_out, not_1_out, b, not_3_out, d);
  and and_12 (and_12_out, and_11_out, d5);
  and and_13 (and_13_out, not_1_out, b, c, not_4_out);
  and and_14 (and_14_out, and_13_out, d6);
  and and_15 (and_15_out, not_1_out, b, c, d);
  and and_16 (and_16_out, and_15_out, d7);
  and and_17 (and_17_out, a, not_2_out, not_3_out, not_4_out);
  and and_18 (and_18_out, and_17_out, d8);
  and and_19 (and_19_out, a, not_2_out, not_3_out, d);
  and and_20 (and_20_out, and_19_out, d9);
  and and_21 (and_21_out, a, not_2_out, c, not_4_out);
  and and_22 (and_22_out, and_21_out, d10);
  and and_23 (and_23_out, a, not_2_out, c, d);
  and and_24 (and_24_out, and_23_out, d11);
  and and_25 (and_25_out, a, b, not_3_out, not_4_out);
  and and_26 (and_26_out, and_25_out, d12);
  and and_27 (and_27_out, a, b, not_3_out, d);
  and and_28 (and_28_out, and_27_out, d13);
  and and_29 (and_29_out, a, b, c, not_4_out);
  and and_30 (and_30_out, and_29_out, d14);
  and and_31 (and_31_out, a, b, c, d);
  and and_32 (and_32_out, and_31_out, d15);
  or or_1 (or_1_out, and_2_out, and_4_out, and_6_out, and_8_out, and_10_out, and_12_out, and_14_out, and_16_out, and_18_out, and_20_out, and_22_out, and_24_out, and_26_out, and_28_out, and_30_out, and_32_out);
  not not_5 (not_5_out, a);
  not not_6 (not_6_out, b);
  not not_7 (not_7_out, c);
  not not_8 (not_8_out, d);
  and and_33 (out_21, or_1_out, not_5_out, not_6_out, not_7_out, not_8_out);
  and and_34 (out_22, or_1_out, not_5_out, not_6_out, not_7_out, d);
  and and_35 (out_23, or_1_out, not_5_out, not_6_out, c, not_8_out);
  and and_36 (out_24, or_1_out, not_5_out, not_6_out, c, d);
  and and_37 (out_25, or_1_out, not_5_out, b, not_7_out, not_8_out);
  and and_38 (out_26, or_1_out, not_5_out, b, not_7_out, d);
  and and_39 (out_27, or_1_out, not_5_out, b, c, not_8_out);
  and and_40 (out_28, or_1_out, not_5_out, b, c, d);
  and and_41 (out_29, or_1_out, a, not_6_out, not_7_out, not_8_out);
  and and_42 (out_30, or_1_out, a, not_6_out, not_7_out, d);
  and and_43 (out_31, or_1_out, a, not_6_out, c, not_8_out);
  and and_44 (out_32, or_1_out, a, not_6_out, c, d);
  and and_45 (out_33, or_1_out, a, b, not_7_out, not_8_out);
  and and_46 (out_34, or_1_out, a, b, not_7_out, d);
  and and_47 (out_35, or_1_out, a, b, c, not_8_out);
  and and_48 (out_36, or_1_out, a, b, c, d);
endmodule
