// Logisim project VT_1.3.circ as structural Verilog: 1 circuit, main circuit main
module main (
  input  x1,
  input  x2,
  input  x3,
  output y1,
  output y2
);

  wire not_1_out, not_2_out, or_1_out;

  not not_1 (not_1_out, x1);
  not not_2 (not_2_out, x2);
  and and_1 (x3, not_1_out, not_2_out);
  or or_1 (or_1_out, x2, x3);
  and and_2 (y1, x3, x3);
  and and_3 (y2, x1, or_1_out);
endmodule
