// Logisim project VT_1.circ as structural Verilog: 1 circuit, main circuit main
module main (
  input  a,
  input  b,
  input  c,
  output y
);

  wire and_1_out, nand_1_out, nand_2_out, nand_3_out, or_1_out;

  nand nand_1 (nand_1_out, b, c);
  nand nand_2 (nand_2_out, a, b);
  or or_1 (or_1_out, nand_1_out, nand_2_out);
  nand nand_3 (nand_3_out, a, or_1_out, c);
  or or_2 (y, nand_3_out, and_1_out);
  and and_1 (and_1_out, a, b, c);
endmodule
