// Logisim project VT_2_2.circ as structural Verilog: 1 circuit, main circuit main
module main (
  input  a,
  input  b,
  input  c,
  input  d,
  output f
);

  wire and_1_out, and_2_out, and_3_out, and_4_out, not_1_out, not_2_out, not_3_out, not_4_out;

  not not_1 (not_1_out, a);
  not not_2 (not_2_out, b);
  not not_3 (not_3_out, c);
  not not_4 (not_4_out, d);
  and and_1 (and_1_out, not_2_out, not_3_out, d);
  and and_2 (and_2_out, not_1_out, c, d);
  and and_3 (and_3_out, a, b, d);
  and and_4 (and_4_out, a, not_2_out, c, not_4_out);
  or or_1 (f, and_1_out, and_2_out, and_3_out, and_4_out);
endmodule
