// Logisim project prac2_3.circ as structural Verilog: 1 circuit, main circuit main
module main (
  input  x0,
  input  x1,
  input  x2,
  input  x3,
  input  x4,
  input  x5,
  input  x6,
  input  x7,
  input  x8,
  input  x9,
  input  x10,
  input  x11,
  input  x12,
  input  x13,
  input  x14,
  input  x15,
  output y1,
  output y2,
  output y3,
  output y4
);

  or or_1 (y1, x1, x3, x5, x9, x11, x13, x15);
  or or_2 (y2, x2, x3, x6, x10, x11, x14, x15);
  or or_3 (y3, x4, x5, x6, x12, x13, x14, x15);
  or or_4 (y4, x8, x9, x10, x11, x12, x13, x14, x15);
endmodule
