// Logisim project prac4_3.circ as structural Verilog: 1 circuit, main circuit main
module main (
  input  x1,
  input  x2,
  input  x3,
  input  x4,
  output y1,
  output y2,
  output y3,
  output y4,
  output y5,
  output y6,
  output y7,
  output y8,
  output y9,
  output y10,
  output y11,
  output y12,
  output y13,
  output y14,
  output y15
);

  wire not_1_out, not_2_out, not_3_out, not_4_out;

  not not_1 (not_1_out, x1);
  not not_2 (not_2_out, x2);
  not not_3 (not_3_out, x3);
  not not_4 (not_4_out, x4);
  and and_1 (y1, not_1_out, not_2_out, not_3_out, not_4_out);
  and and_2 (y2, x1, not_2_out, not_3_out, not_4_out);
  and and_3 (y3, not_1_out, x2, not_3_out, not_4_out);
  and and_4 (y4, x1, x2, not_3_out, not_4_out);
  and and_5 (y5, not_1_out, not_2_out, x3, not_4_out);
  and and_6 (y6, x1, not_2_out, x3, not_4_out);
  and and_7 (y8, not_1_out, not_2_out, not_3_out, x4);
  and and_8 (y9, x1, not_2_out, not_3_out, x4);
  and and_9 (y10, not_1_out, x2, not_3_out, x4);
  and and_10 (y11, x1, x2, not_3_out, x4);
  and and_11 (y12, not_1_out, not_2_out, x3, x4);
  and and_12 (y13, x1, not_2_out, x3, x4);
  and and_13 (y14, not_1_out, x2, x3, x4);
  and and_14 (y15, x1, x2, x3, x4);

  assign y7 = 1'b0;
endmodule
