// Logisim project prac5_1.circ as structural Verilog: 1 circuit, main circuit main
module main (
  input  a,
  input  b,
  input  c,
  input  d,
  output E
);

  wire and_1_out, and_2_out, and_3_out, and_4_out, and_5_out, and_6_out, and_7_out, and_8_out, and_9_out,
       and_10_out, and_11_out, and_12_out, and_13_out, and_14_out, and_15_out, and_16_out, not_1_out,
       not_2_out, not_3_out, not_4_out;

  not not_1 (not_1_out, a);
  not not_2 (not_2_out, b);
  not not_3 (not_3_out, c);
  not not_4 (not_4_out, d);
  and and_1 (and_1_out, 1'b0, not_1_out, not_2_out, not_3_out, not_4_out);
  and and_2 (and_2_out, 1'b0, not_1_out, not_2_out, not_3_out, d);
  and and_3 (and_3_out, 1'b1, not_1_out, not_2_out, c, not_4_out);
  and and_4 (and_4_out, 1'b1, not_1_out, not_2_out, c, d);
  and and_5 (and_5_out, 1'b0, not_1_out, b, not_3_out, not_4_out);
  and and_6 (and_6_out, 1'b0, not_1_out, b, not_3_out, d);
  and and_7 (and_7_out, 1'b1, not_1_out, b, c, not_4_out);
  and and_8 (and_8_out, 1'b1, not_1_out, b, c, d);
  and and_9 (and_9_out, 1'b0, a, not_2_out, not_3_out, not_4_out);
  and and_10 (and_10_out, 1'b1, a, not_2_out, not_3_out, d);
  and and_11 (and_11_out, 1'b1, a, not_2_out, c, not_4_out);
  and and_12 (and_12_out, 1'b0, a, not_2_out, c, d);
  and and_13 (and_13_out, 1'b0, a, b, not_3_out, not_4_out);
  and and_14 (and_14_out, 1'b1, a, b, not_3_out, d);
  and and_15 (and_15_out, 1'b0, a, b, c, not_4_out);
  and and_16 (and_16_out, 1'b1, a, b, c, d);
  or or_1 (E, and_1_out, and_2_out, and_3_out, and_4_out, and_5_out, and_6_out, and_7_out, and_8_out, and_9_out, and_10_out, and_11_out, and_12_out, and_13_out, and_14_out, and_15_out, and_16_out);
endmodule
